# Fritzing sketch capacitanceKeyboard (saved by Fritzing 0.9.4)
breadboards: 1

parts:
  R1 = Resistor [tolerance=±5% resistance=22M package=THT]
  R3 = Resistor [tolerance=±5% resistance=22M package=THT]
  R4 = Resistor [tolerance=±5% resistance=22M package=THT]
  R5 = Resistor [tolerance=±5% resistance=22M package=THT]
  R6 = Resistor [tolerance=±5% resistance=22M package=THT]
  R7 = Resistor [tolerance=±5% resistance=22M package=THT]
  R8 = Resistor [tolerance=±5% resistance=22M package=THT]
  R9 = Resistor [tolerance=±5% resistance=22M package=THT]
  R10 = Trimmer Potentiometer [maximum_resistance=10kΩ package=THT]
  Pro_Micro1 = SparkFun Pro Micro
  J4 = male pin header, 1 pin [form="♂ (male)"]
  J5 = male pin header, 1 pin [form="♂ (male)"]
  J6 = male pin header, 1 pin [form="♂ (male)"]
  J7 = male pin header, 1 pin [form="♂ (male)"]
  J8 = male pin header, 1 pin [form="♂ (male)"]
  J9 = male pin header, 1 pin [form="♂ (male)"]
  J10 = male pin header, 1 pin [form="♂ (male)"]
  J11 = male pin header, 1 pin [form="♂ (male)"]
  SW1 = DIP SWITCH [package=dipswitch-02]
  SW2 = DIP SWITCH [package=dipswitch-02]

nets:
  N1: R1.Pin_0, R3.Pin_0, R4.Pin_0, R5.Pin_0, R6.Pin_1, R7.Pin_1, R8.Pin_1, R9.Pin_1, R10.leg2, Pro_Micro1.VCC, SW1.3, SW1.4, SW2.3, SW2.4
  N2: R1.Pin_1, Pro_Micro1.8, J10.pin1
  N3: R3.Pin_1, Pro_Micro1.6, J9.pin1
  N4: R4.Pin_1, Pro_Micro1.4, J4.pin1
  N5: R5.Pin_1, Pro_Micro1.9, J11.pin1
  N6: R6.Pin_0, Pro_Micro1.A3, J8.pin1
  N7: R7.Pin_0, Pro_Micro1.A2, J7.pin1
  N8: R8.Pin_0, Pro_Micro1.A1, J6.pin1
  N9: R9.Pin_0, Pro_Micro1.A0, J5.pin1
  N10: R10.leg1, Pro_Micro1.GND
  N11: R10.wiper, Pro_Micro1.10
  N12: Pro_Micro1.2, SW1.1
  N13: Pro_Micro1.3, SW1.2
  N14: Pro_Micro1.5, SW2.2

custom parts:
  SparkFun Pro Micro: The Pro Micro is similar to the Pro Mini except with an ATmega32U4 on board. The USB transceiver inside the 32U4 allows us to add USB connectivity on-board and do away with bulky external USB interface. Based on: https://github.com/unorthodox-engineers/unorthodox-arduino/blob/master/Unorthodox/fritzing/parts/Pro%20Micro.fzpz
